// Logisim project cpu_evolution.circ as structural Verilog: 11 circuits, main circuit CPU
module main (
  input  irq,
  input  [15:0] in_2,
  input  in_3,
  input  in_4,
  input  in_5,
  output [7:0] out_6
);

  wire and_1_out, and_2_out, and_3_out, clock_1_out, cpu_1_rd, cpu_1_wr, not_1_out, not_2_out;
  wire [6:0] cpu_1_d_out;
  wire [7:0] controlled_buffer_3_out, register_1_q, rom_1_data;
  wire [7:7] cpu_1_d_out_2;
  wire [17:0] cpu_1_a;

  Clock clock_1 (.out(clock_1_out));
  CPU cpu_1 (
    .wr(cpu_1_wr), .rd(cpu_1_rd), .d_out({cpu_1_d_out_2[7], cpu_1_d_out}), .a(cpu_1_a),
    .d_in({cpu_1_d_out_2[7], cpu_1_d_out}), .irq(irq), .clock(not_1_out));
  not not_1 (not_1_out, clock_1_out);
  TTY tty_1 (.data(cpu_1_d_out), .clk(not_1_out), .we(cpu_1_a[17]));  // open: clr
  assign {cpu_1_d_out_2[7], cpu_1_d_out} = not_2_out ? rom_1_data : 8'bz;  // Controlled_Buffer controlled_buffer_1
  not not_2 (not_2_out, cpu_1_a[16]);
  and and_1 (and_1_out, cpu_1_rd, cpu_1_a[16]);
  and and_2 (and_2_out, cpu_1_wr, cpu_1_a[16]);
  assign {cpu_1_d_out_2[7], cpu_1_d_out} = and_1_out ? controlled_buffer_3_out : 8'bz;  // Controlled_Buffer controlled_buffer_2
  Register register_1 (.D({cpu_1_d_out_2[7], cpu_1_d_out}), .Q(register_1_q), .clk(and_3_out));  // open: en, clr
  and and_3 (and_3_out, and_2_out, not_1_out);
  assign controlled_buffer_3_out = and_2_out ? register_1_q : 8'bz;  // Controlled_Buffer controlled_buffer_3
  ROM #(.addrWidth(16)) rom_1 (.addr(cpu_1_a[15:0]), .data(rom_1_data));
  RAM #(.addrWidth(16), .databus("bidir"), .trigger("falling")) ram_1 (
    .addr(cpu_1_a[15:0]), .we(and_2_out), .oe(and_1_out), .clk(not_1_out), .data(controlled_buffer_3_out));
  Pull_Resistor pull_resistor_1 (.node(controlled_buffer_3_out));
  RAM #(.addrWidth(16), .databus("bidir")) ram_2 (.addr(in_2), .we(in_3), .oe(in_4), .clk(in_5), .data(out_6));

  // Notes on the sheet:
  //   contents of rom_1 (hex, n*v repeats v):
  //   2b 2b 2b
endmodule

module CPU (
  input  [7:0] d_in,
  input  irq,
  input  clock,
  output wr,
  output rd,
  output [7:0] d_out,
  output [17:0] a
);

  wire alu_1_c_out, alu_1_sf_out, alu_1_vf_out, alu_1_zf_out, flags_1_cf_out, mid_1_cnd, mid_1_cs, mid_1_dec,
       mid_1_ds, mid_1_ec, mid_1_feo, mid_1_fws, mid_1_goe, mid_1_gwe, mid_1_he, mid_1_inc_ip, mid_1_inc_sp,
       mid_1_inv, mid_1_nxt, mid_1_rl, mid_1_rr, mid_1_sa, mid_1_soe, mid_1_swe;
  wire [1:0] mid_1_grs, mid_1_gws, mid_1_hs, mid_1_op;
  wire [2:0] mid_1_srs, mid_1_sws;
  wire [7:0] A_t, alu_1_c, B, F, flags_1_cu_out, grf_1_abus, grf_1_y_out, MD, mid_1_cu_fs, mid_1_fs,
       srf_1_bbus, srf_1_iph_out, srf_1_md_out, srf_1_sph_out, srf_1_ss_out, srf_1_tmph_out, SS, X, Y;
  wire [11:0] cu_1_mip_out, mid_1_cnd_nmip, mid_1_nmip;
  wire [15:0] inc_1_inc_res, IP, SP, srf_1_inc_in, TMP;
  wire [55:0] rom_1_data;

  // Probe on F
  // Probe on B
  // Probe on IP
  // Probe on MD
  // Probe on Y
  // Probe on A_t
  // Probe on SP
  // Probe on X
  // Probe on TMP
  // Probe on SS
  MID mid_1 (
    .grs(mid_1_grs), .rr(mid_1_rr), .rl(mid_1_rl), .op(mid_1_op), .inv(mid_1_inv), .ec(mid_1_ec),
    .sa(mid_1_sa), .feo(mid_1_feo), .fs(mid_1_fs), .fws(mid_1_fws), .sws(mid_1_sws), .swe(mid_1_swe),
    .srs(mid_1_srs), .soe(mid_1_soe), .inc_sp(mid_1_inc_sp), .inc_ip(mid_1_inc_ip), .dec(mid_1_dec),
    .ds(mid_1_ds), .cs(mid_1_cs), .he(mid_1_he), .goe(mid_1_goe), .hs(mid_1_hs), .wr(wr), .cnd(mid_1_cnd),
    .rd(rd), .nxt(mid_1_nxt), .nmip(mid_1_nmip), .cnd_nmip(mid_1_cnd_nmip), .gwe(mid_1_gwe),
    .CU_fs(mid_1_cu_fs), .gws(mid_1_gws), .mi(rom_1_data));
  assign d_out = wr ? srf_1_md_out : 8'bz;  // Controlled_Buffer controlled_buffer_1
  ADDR addr_1 (
    .adr(a), .ss(srf_1_ss_out), .cbus(alu_1_c), .iph(srf_1_iph_out), .sph(srf_1_sph_out),
    .tmph(srf_1_tmph_out), .y(grf_1_y_out), .hs(mid_1_hs), .he(mid_1_he), .cs(mid_1_cs), .ds(mid_1_ds));
  // Probe on cu_1_mip_out
  CU cu_1 (
    .mip_out(cu_1_mip_out), .flags(flags_1_cu_out), .fsel(mid_1_cu_fs), .cnd(mid_1_cnd), .nmip(mid_1_nmip),
    .cnd_nmip(mid_1_cnd_nmip), .md(srf_1_md_out), .nxt(mid_1_nxt), .clock(clock));
  ROM #(.addrWidth(12), .dataWidth(56)) rom_1 (.addr(cu_1_mip_out), .data(rom_1_data));
  INC inc_1 (.inc_res(inc_1_inc_res), .inc_in(srf_1_inc_in), .dec(mid_1_dec));
  SRF srf_1 (
    .ddmd(MD), .md_out(srf_1_md_out), .ddss(SS), .ss_out(srf_1_ss_out), .bbus(srf_1_bbus), .ddip(IP),
    .iph_out(srf_1_iph_out), .ddsp(SP), .inc_in(srf_1_inc_in), .sph_out(srf_1_sph_out), .ddtmp(TMP),
    .tmph_out(srf_1_tmph_out), .swe(mid_1_swe), .srs(mid_1_srs), .soe(mid_1_soe), .cbus(alu_1_c),
    .sws(mid_1_sws), .inc_ip(mid_1_inc_ip), .clock(clock), .inc_res(inc_1_inc_res), .inc_sp(mid_1_inc_sp),
    .wr(rd), .md_in(d_in));
  FLAGS flags_1 (
    .cf_out(flags_1_cf_out), .cbus_out(srf_1_bbus), .ddf(F), .cu_out(flags_1_cu_out), .cf_in(alu_1_c_out),
    .zf_in(alu_1_zf_out), .sf_in(alu_1_sf_out), .vf_in(alu_1_vf_out), .irq(irq), .fws(mid_1_fws),
    .cbus_in(alu_1_c), .fs(mid_1_fs), .clock(clock), .ec(mid_1_ec), .sa(mid_1_sa), .feo(mid_1_feo));
  ALU alu_1 (
    .vf_out(alu_1_vf_out), .sf_out(alu_1_sf_out), .c(alu_1_c), .c_out(alu_1_c_out), .zf_out(alu_1_zf_out),
    .c_in(flags_1_cf_out), .a(grf_1_abus), .b(srf_1_bbus), .inv(mid_1_inv), .rl(mid_1_rl), .rr(mid_1_rr),
    .op(mid_1_op));
  GRF grf_1 (
    .y_out(grf_1_y_out), .abus(grf_1_abus), .ddb(B), .dda(A_t), .ddy(Y), .ddx(X), .cbus(alu_1_c),
    .goe(mid_1_goe), .gwe(mid_1_gwe), .gws(mid_1_gws), .grs(mid_1_grs), .clock(clock));

  // Notes on the sheet:
  //   DEBUG INFO
  //   E
  //   A
  //   V
  //   S
  //   Z
  //   C
  //   P
  //   I
  //   contents of rom_1 (hex, n*v repeats v):
  //   0 3e61840000000 300007802000 100000440400 10010000082b 10010000082b 700177001800 10f400000031 35*0
  //   627400000031 16*0 50000000583f 0 40000000583f 4032*0 200000410400
endmodule

module SRF (
  input  swe,
  input  [2:0] sws,
  input  inc_ip,
  input  inc_sp,
  input  wr,
  input  [2:0] srs,
  input  soe,
  input  [7:0] cbus,
  input  clock,
  input  [15:0] inc_res,
  input  [7:0] md_in,
  output [7:0] ddmd,
  output [7:0] ddss,
  output [15:0] ddip,
  output [15:0] ddsp,
  output [15:0] ddtmp,
  output [7:0] md_out,
  output [7:0] bbus,
  output [7:0] iph_out,
  output [15:0] inc_in,
  output [7:0] sph_out,
  output [7:0] tmph_out,
  output [7:0] ss_out
);

  wire decoder_1_out0, decoder_1_out1, decoder_1_out2, decoder_1_out3, decoder_1_out4, decoder_1_out5,
       decoder_1_out6, decoder_1_out7, hls_1_wh_out, hls_1_wl_out, hls_2_wh_out, hls_2_wl_out, or_1_out;
  wire [7:0] hls_1_high_out, hls_1_low_out, hls_2_high_out, hls_2_low_out, multiplexer_1_out,
       multiplexer_2_out;

  Decoder #(.select(3)) decoder_1 (
    .out0(decoder_1_out0), .out1(decoder_1_out1), .out2(decoder_1_out2), .out3(decoder_1_out3),
    .out4(decoder_1_out4), .out5(decoder_1_out5), .out6(decoder_1_out6), .out7(decoder_1_out7), .sel(sws),
    .en(swe));
  Register IPL (.D(hls_1_low_out), .en(hls_1_wl_out), .Q(ddip[7:0]), .clk(clock));  // open: clr
  HLS hls_1 (
    .low_out(hls_1_low_out), .wl_out(hls_1_wl_out), .high_out(hls_1_high_out), .wh_out(hls_1_wh_out),
    .wl(decoder_1_out0), .wh(decoder_1_out1), .inc_res(inc_res), .c_bus(cbus), .inc(inc_ip));
  Register IPH (.D(hls_1_high_out), .en(hls_1_wh_out), .Q(ddip[15:8]), .clk(clock));  // open: clr
  Register SPL (.D(hls_2_low_out), .en(hls_2_wl_out), .Q(ddsp[7:0]), .clk(clock));  // open: clr
  HLS hls_2 (
    .low_out(hls_2_low_out), .wl_out(hls_2_wl_out), .high_out(hls_2_high_out), .wh_out(hls_2_wh_out),
    .wl(decoder_1_out2), .wh(decoder_1_out3), .inc_res(inc_res), .c_bus(cbus), .inc(inc_sp));
  Register SPH (.D(hls_2_high_out), .en(hls_2_wh_out), .Q(ddsp[15:8]), .clk(clock));  // open: clr
  assign inc_in = inc_ip ? ddip : 16'bz;  // Controlled_Buffer controlled_buffer_1
  assign inc_in = inc_sp ? ddsp : 16'bz;  // Controlled_Buffer controlled_buffer_2
  Register TMPL (.D(cbus), .en(decoder_1_out4), .Q(ddtmp[7:0]), .clk(clock));  // open: clr
  Register TMPH (.D(cbus), .en(decoder_1_out5), .Q(ddtmp[15:8]), .clk(clock));  // open: clr
  Register #(.trigger("falling")) MD (.D(multiplexer_1_out), .en(or_1_out), .Q(ddmd), .clk(clock));  // open: clr
  or or_1 (or_1_out, decoder_1_out6, wr);
  Multiplexer #(.width(8)) multiplexer_1 (.in0(cbus), .in1(md_in), .out(multiplexer_1_out), .sel(wr));
  Register SS (.D(cbus), .en(decoder_1_out7), .Q(ddss), .clk(clock));  // open: clr
  Multiplexer #(.select(3), .width(8)) multiplexer_2 (
    .in0(ddip[7:0]), .in1(ddip[15:8]), .in2(ddsp[7:0]), .in3(ddsp[15:8]), .in4(ddtmp[7:0]),
    .in5(ddtmp[15:8]), .in6(ddmd), .in7(ddss), .out(multiplexer_2_out), .sel(srs));
  assign bbus = soe ? multiplexer_2_out : 8'bz;  // Controlled_Buffer controlled_buffer_3

  assign iph_out = ddip[15:8];
  assign md_out = ddmd;
  assign sph_out = ddsp[15:8];
  assign ss_out = ddss;
  assign tmph_out = ddtmp[15:8];
endmodule

module GRF (
  input  goe,
  input  gwe,
  input  [1:0] gws,
  input  [1:0] grs,
  input  [7:0] cbus,
  input  clock,
  output [7:0] y_out,
  output [7:0] ddb,
  output [7:0] abus,
  output [7:0] dda,
  output [7:0] ddy,
  output [7:0] ddx
);

  wire decoder_1_out0, decoder_1_out1, decoder_1_out2, decoder_1_out3;
  wire [7:0] multiplexer_1_out;

  assign abus = goe ? multiplexer_1_out : 8'bz;  // Controlled_Buffer controlled_buffer_1
  Multiplexer #(.select(2), .width(8)) multiplexer_1 (
    .in0(ddb), .in1(dda), .in2(ddy), .in3(ddx), .out(multiplexer_1_out), .sel(grs));
  Decoder #(.select(2)) decoder_1 (
    .out0(decoder_1_out0), .out1(decoder_1_out1), .out2(decoder_1_out2), .out3(decoder_1_out3), .sel(gws),
    .en(gwe));
  Register B (.D(cbus), .en(decoder_1_out0), .Q(ddb), .clk(clock));  // open: clr
  Register A (.D(cbus), .en(decoder_1_out1), .Q(dda), .clk(clock));  // open: clr
  Register Y (.D(cbus), .en(decoder_1_out2), .Q(ddy), .clk(clock));  // open: clr
  Register X (.D(cbus), .en(decoder_1_out3), .Q(ddx), .clk(clock));  // open: clr

  assign y_out = ddy;
endmodule

module HLS (
  input  inc,
  input  wl,
  input  wh,
  input  [15:0] inc_res,
  input  [7:0] c_bus,
  output [7:0] low_out,
  output wl_out,
  output [7:0] high_out,
  output wh_out
);

  Multiplexer #(.width(8)) multiplexer_1 (.in0(c_bus), .in1(inc_res[7:0]), .out(low_out), .sel(inc));
  or or_1 (wl_out, wl, inc);
  Multiplexer #(.width(8)) multiplexer_2 (.in0(c_bus), .in1(inc_res[15:8]), .out(high_out), .sel(inc));
  or or_2 (wh_out, wh, inc);
endmodule

module ALU (
  input  [1:0] op,
  input  c_in,
  input  [7:0] a,
  input  [7:0] b,
  input  inv,
  input  rl,
  input  rr,
  output vf_out,
  output sf_out,
  output [7:0] c,
  output c_out,
  output zf_out
);

  wire adder_1_cout, nor_1_out, or_1_out;
  wire [7:0] adder_1_out, and_1_out, bit_extender_1_out, multiplexer_1_out, or_2_out, xor_1_out, xor_2_out;

  assign bit_extender_1_out = {{7{inv}}, inv};  // Bit_Extender bit_extender_1
  assign xor_1_out = b ^ bit_extender_1_out;  // XOR_Gate xor_1, 8 bits wide
  or or_1 (or_1_out, a[7], xor_1_out[7]);
  Adder adder_1 (.a(a), .b(xor_1_out), .out(adder_1_out), .cin(c_in), .cout(adder_1_cout));
  assign or_2_out = a | xor_1_out;  // OR_Gate or_2, 8 bits wide
  assign and_1_out = a & xor_1_out;  // AND_Gate and_1, 8 bits wide
  assign xor_2_out = a ^ xor_1_out;  // XOR_Gate xor_2, 8 bits wide
  Multiplexer #(.select(2), .width(8)) multiplexer_1 (
    .in0(adder_1_out), .in1(or_2_out), .in2(and_1_out), .in3(xor_2_out), .out(multiplexer_1_out), .sel(op));
  assign c_out = nor_1_out ? adder_1_cout : 1'bz;  // Controlled_Buffer controlled_buffer_1
  assign c = rr ? {multiplexer_1_out[0], multiplexer_1_out[7:1]} : 8'bz;  // Controlled_Buffer controlled_buffer_2
  assign c_out = rr ? multiplexer_1_out[0] : 1'bz;  // Controlled_Buffer controlled_buffer_3
  assign c_out = rl ? multiplexer_1_out[7] : 1'bz;  // Controlled_Buffer controlled_buffer_4
  assign c = rl ? {multiplexer_1_out[6:0], multiplexer_1_out[7]} : 8'bz;  // Controlled_Buffer controlled_buffer_5
  assign c = nor_1_out ? multiplexer_1_out : 8'bz;  // Controlled_Buffer controlled_buffer_6
  nor nor_1 (nor_1_out, rl, rr);
  xor xor_3 (vf_out, or_1_out, c[7]);
  nor nor_2 (zf_out, c[0], c[1], c[2], c[3], c[4], c[5], c[6], c[7]);

  assign sf_out = c[7];
endmodule

module ADDR (
  input  [1:0] hs,
  input  he,
  input  cs,
  input  ds,
  input  [7:0] ss,
  input  [7:0] cbus,
  input  [7:0] iph,
  input  [7:0] sph,
  input  [7:0] tmph,
  input  [7:0] y,
  output [17:0] adr
);

  wire [3:0] controlled_buffer_2_out;
  wire [7:0] multiplexer_1_out;
  wire [15:14] controlled_buffer_1_out;

  assign {controlled_buffer_1_out, adr[13:8]} = he ? multiplexer_1_out : 8'bz;  // Controlled_Buffer controlled_buffer_1
  Multiplexer #(.select(2), .width(8)) multiplexer_1 (
    .in0(iph), .in1(sph), .in2(tmph), .in3(y), .out(multiplexer_1_out), .sel(hs));
  assign controlled_buffer_2_out = ds ? ss[3:0] : 4'bz;  // Controlled_Buffer controlled_buffer_2
  assign controlled_buffer_2_out = cs ? ss[7:4] : 4'bz;  // Controlled_Buffer controlled_buffer_3
  Pull_Resistor pull_resistor_1 (.node({controlled_buffer_1_out, adr[13:8]}));
  Adder #(.width(4)) adder_1 (
    .a(controlled_buffer_2_out), .b({2'b00, controlled_buffer_1_out}), .out(adr[17:14]));  // open: cin, cout
  Pull_Resistor pull_resistor_2 (.node({adr[17:8], cbus}));

  assign adr[7:0] = cbus;
endmodule

module FLAGS (
  input  fws,
  input  [7:0] cbus_in,
  input  [7:0] fs,
  input  ec,
  input  sa,
  input  feo,
  input  cf_in,
  input  zf_in,
  input  sf_in,
  input  vf_in,
  input  irq,
  input  clock,
  output cf_out,
  output [7:0] cbus_out,
  output [7:0] ddf,
  output [7:0] cu_out
);

  wire and_1_out, and_2_out, and_3_out, and_4_out, and_5_out, and_6_out, and_7_out, and_8_out, and_9_out,
       I_qn, multiplexer_1_out, multiplexer_2_out, multiplexer_3_out, multiplexer_4_out, multiplexer_5_out,
       or_1_out, or_2_out, or_3_out;

  Multiplexer multiplexer_1 (.in0(cf_in), .in1(cbus_in[0]), .out(multiplexer_1_out), .sel(fws));
  Multiplexer multiplexer_2 (.in0(zf_in), .in1(cbus_in[1]), .out(multiplexer_2_out), .sel(fws));
  Multiplexer multiplexer_3 (.in0(sf_in), .in1(cbus_in[2]), .out(multiplexer_3_out), .sel(fws));
  Multiplexer multiplexer_4 (.in0(vf_in), .in1(cbus_in[3]), .out(multiplexer_4_out), .sel(fws));
  or or_1 (or_1_out, fs[6], and_1_out);
  and and_1 (and_1_out, cu_out[5], irq);
  or or_2 (or_2_out, irq, cbus_in[6]);
  and and_2 (and_2_out, fs[0], clock);
  and and_3 (and_3_out, fs[1], clock);
  and and_4 (and_4_out, fs[2], clock);
  and and_5 (and_5_out, fs[3], clock);
  and and_6 (and_6_out, fs[4], clock);
  or or_3 (or_3_out, multiplexer_1_out, cbus_in[4]);
  and and_7 (and_7_out, fs[5], clock);
  and and_8 (and_8_out, fs[7], clock);
  and and_9 (and_9_out, or_1_out, clock);
  and and_10 (cf_out, ec, multiplexer_5_out);
  Multiplexer multiplexer_5 (.in0(cu_out[0]), .in1(cu_out[4]), .out(multiplexer_5_out), .sel(sa));
  D_Flip_Flop C (.clk(and_2_out), .D(multiplexer_1_out), .Q(cu_out[0]));  // open: Qn, preset, reset
  D_Flip_Flop Z (.clk(and_3_out), .D(multiplexer_2_out), .Q(cu_out[1]));  // open: Qn, preset, reset
  D_Flip_Flop S (.clk(and_4_out), .D(multiplexer_3_out), .Q(cu_out[2]));  // open: Qn, preset, reset
  D_Flip_Flop V (.clk(and_5_out), .D(multiplexer_4_out), .Q(cu_out[3]));  // open: Qn, preset, reset
  D_Flip_Flop AC (.clk(and_6_out), .D(or_3_out), .Q(cu_out[4]));  // open: Qn, preset, reset
  D_Flip_Flop E (.clk(and_7_out), .D(cbus_in[5]), .Q(cu_out[5]));  // open: Qn, preset, reset
  D_Flip_Flop P (.clk(and_8_out), .D(cbus_in[7]), .Q(cu_out[6]));  // open: Qn, preset, reset
  D_Flip_Flop I (.clk(and_9_out), .D(or_2_out), .Q(cu_out[7]), .Qn(I_qn));  // open: preset, reset
  assign cbus_out = feo ? cu_out : 8'bz;  // Controlled_Buffer controlled_buffer_1

  assign ddf = cu_out;
endmodule

module INC (
  input  [15:0] inc_in,
  input  dec,
  output [15:0] inc_res
);

  wire [15:0] bit_extender_1_out, xor_1_out;

  assign bit_extender_1_out = {{15{dec}}, dec};  // Bit_Extender bit_extender_1
  assign xor_1_out = 16'h1 ^ bit_extender_1_out;  // XOR_Gate xor_1, 16 bits wide
  Adder #(.width(16)) adder_1 (.a(inc_in), .b(xor_1_out), .out(inc_res), .cin(dec));  // open: cout
endmodule

module CU (
  input  [7:0] flags,
  input  [7:0] fsel,
  input  cnd,
  input  [11:0] nmip,
  input  [11:0] cnd_nmip,
  input  clock,
  input  [7:0] md,
  input  nxt,
  output [11:0] mip_out
);

  wire and_2_out, or_1_out;
  wire [7:0] and_1_out;
  wire [11:0] MIP_q, multiplexer_1_out, multiplexer_2_out, not_1_out;

  assign and_1_out = flags & fsel;  // AND_Gate and_1, 8 bits wide
  or or_1 (or_1_out, and_1_out[0], and_1_out[1], and_1_out[2], and_1_out[3], and_1_out[4], and_1_out[5], and_1_out[6], and_1_out[7]);
  and and_2 (and_2_out, cnd, or_1_out);
  Multiplexer #(.width(12)) multiplexer_1 (.in0(nmip), .in1(cnd_nmip), .out(multiplexer_1_out), .sel(and_2_out));
  assign not_1_out = ~multiplexer_2_out;  // NOT_Gate not_1, 12 bits wide
  Multiplexer #(.width(12)) multiplexer_2 (
    .in0(multiplexer_1_out), .in1({flags[6], 3'b000, md}), .out(multiplexer_2_out), .sel(nxt));
  assign mip_out = ~MIP_q;  // NOT_Gate not_2, 12 bits wide
  Register #(.width(12)) MIP (.D(not_1_out), .Q(MIP_q), .clk(clock));  // open: en, clr
endmodule

module MID (
  input  [55:0] mi,
  output goe,
  output gwe,
  output [1:0] gws,
  output [1:0] grs,
  output rr,
  output rl,
  output [1:0] op,
  output inv,
  output ec,
  output sa,
  output feo,
  output [7:0] fs,
  output fws,
  output [2:0] sws,
  output swe,
  output [2:0] srs,
  output soe,
  output inc_sp,
  output inc_ip,
  output dec,
  output ds,
  output cs,
  output he,
  output [1:0] hs,
  output wr,
  output cnd,
  output rd,
  output nxt,
  output [11:0] nmip,
  output [11:0] cnd_nmip,
  output [7:0] CU_fs
);

  wire [11:0] bit_extender_1_out;

  assign {ec, inv, op, rl, rr, grs, gws, gwe, goe} = mi[11:0] & ~bit_extender_1_out;  // AND_Gate and_1, 12 bits wide
  assign bit_extender_1_out = {{11{mi[40]}}, mi[40]};  // Bit_Extender bit_extender_1

  assign cnd = mi[40];
  assign cnd_nmip = mi[11:0];
  assign cs = mi[35];
  assign CU_fs = mi[21:14];
  assign dec = mi[33];
  assign ds = mi[34];
  assign feo = mi[13];
  assign fs = mi[21:14];
  assign fws = mi[22];
  assign he = mi[36];
  assign hs = mi[38:37];
  assign inc_ip = mi[32];
  assign inc_sp = mi[31];
  assign nmip = mi[55:44];
  assign nxt = mi[42];
  assign rd = mi[41];
  assign sa = mi[12];
  assign soe = mi[30];
  assign srs = mi[29:27];
  assign swe = mi[26];
  assign sws = mi[25:23];
  assign wr = mi[39];

  // Notes on the sheet:
  //   RESERVED
endmodule
